// Logisim project 20211019101041C00CE89B18C31C__circuitos.circ as structural Verilog
module gates (
  input  entrada_1,
  input  entrada_2,
  input  entrada_1_2,
  input  entrada_2_2,
  input  entrada,
  output salida,
  output salida_2,
  output salida_3
);

  and and_1 (salida, entrada_1, entrada_2);
  or or_1 (salida_2, entrada_1_2, entrada_2_2);
  not not_1 (salida_3, entrada);

  // Notes on the sheet:
  //   Compuertas básicas
  //   And
  //   Or
  //   Not
endmodule

module _2_bit_adder (
  input  x,
  input  y,
  output w0,
  output w1
);

  xor xor_1 (w0, x, y);
  and and_1 (w1, y, x);

  // Notes on the sheet:
  //   Sumador de 2 bits
  //   El resultado es el nº binario con bits w1 w0
  //   Una salida se puede conectar a varias entradas
  //   pero nunca conecte 2 salidas
  //   porque se produce un cortocircuito
endmodule

module _3_bit_adder (
  input  x,
  input  y,
  input  z,
  output w0,
  output w1
);

  wire n2_bit_adder_1_w0, n2_bit_adder_1_w1, n2_bit_adder_2_w1;

  _2_bit_adder u_2_bit_adder_1 (.x(x), .y(y), .w0(n2_bit_adder_1_w0), .w1(n2_bit_adder_1_w1));
  _2_bit_adder u_2_bit_adder_2 (.x(n2_bit_adder_1_w0), .y(z), .w0(w0), .w1(n2_bit_adder_2_w1));
  or or_1 (w1, n2_bit_adder_2_w1, n2_bit_adder_1_w1);

  // Notes on the sheet:
  //   Sumador de 3 bits
endmodule

module _2_x_4_bit_adder (
  input  [3:0] x3_x0,
  input  [3:0] y3_y0,
  output [3:0] w3_w0,
  output carry
);

  wire n2_bit_adder_1_w1, n3_bit_adder_1_w1, n3_bit_adder_2_w1;

  // Probe on x3_x0
  // Probe on y3_y0
  _2_bit_adder u_2_bit_adder_1 (.x(x3_x0[0]), .y(y3_y0[0]), .w0(w3_w0[0]), .w1(n2_bit_adder_1_w1));
  _3_bit_adder u_3_bit_adder_1 (
    .x(n2_bit_adder_1_w1), .y(x3_x0[1]), .z(y3_y0[1]), .w0(w3_w0[1]), .w1(n3_bit_adder_1_w1));
  _3_bit_adder u_3_bit_adder_2 (
    .x(n3_bit_adder_1_w1), .y(x3_x0[2]), .z(y3_y0[2]), .w0(w3_w0[2]), .w1(n3_bit_adder_2_w1));
  _3_bit_adder u_3_bit_adder_3 (.x(n3_bit_adder_2_w1), .y(x3_x0[3]), .z(y3_y0[3]), .w0(w3_w0[3]), .w1(carry));
  // Probe on w3_w0

  // Notes on the sheet:
  //   Las entradas pueden aceptar múltiples bits
  //   Separador
  //   Sumador de 2 números de 4 bits
  //   Las salidas puede generar múltiples bits
  //   Una línea puede contener múltiples bits
  //   pero se debe conectar a entrada y salidas
  //   de la misma cantidad de bits
  //   Un separador permite seleccionar bits específicos de una línea
endmodule

module \aritmética  (
  input  [7:0] x,
  input  [7:0] y,
  input  [7:0] x_2,
  input  [7:0] a,
  input  [7:0] y_2,
  input  [7:0] b,
  input  [7:0] x_3,
  input  [7:0] c,
  input  [2:0] y_3,
  input  [7:0] d,
  input  [7:0] x_4,
  input  [7:0] y_4,
  output [7:0] w,
  output [7:0] w_2,
  output [7:0] e,
  output f,
  output [7:0] w_3,
  output x_y,
  output x_y_2,
  output x_y_3
);

  wire [2:0] bit_extender_1_out;
  wire [7:0] shifter_2_out, x8_out;

  Adder adder_1 (.a(x), .b(y), .out(w));  // open: cin, cout
  Subtractor subtractor_1 (.a(x_2), .b(y_2), .out(w_2));  // open: bin, bout
  Shifter shifter_1 (.in(x_3), .\dist (y_3), .out(w_3));
  Comparator comparator_1 (.a(x_4), .b(y_4), .gt(x_y), .eq(x_y_2), .lt(x_y_3));
  Bit_Extender #(.out_width(3)) bit_extender_1 (.in(b), .out(bit_extender_1_out));
  Shifter shifter_2 (.in(a), .\dist (bit_extender_1_out), .out(shifter_2_out));
  assign x8_out = c & d;  // AND_Gate x8, 8 bits wide
  Adder adder_2 (.a(shifter_2_out), .b(x8_out), .out(e), .cin(1'b1), .cout(f));

  // Notes on the sheet:
  //   Aritmética
  //   Sumador
  //   Restador
  //   Desplazador a la izquierda
  //   o derecha con o sin signo
  //   Comparador con o sin signo
  //   Ejemplo: (a << b ) + ( c & d ) + 1
  //   Logisim no tiene punto flotante
  //   Los enteros pueden ser de 1 a 32 bits
endmodule

module elementos_modulares (
  input  [7:0] Entrada,
  input  Escribir,
  input  [7:0] x,
  input  start,
  input  reloj,
  input  [7:0] Entrada_0,
  input  [7:0] Entrada_1,
  input  Selector,
  output [7:0] Valor_almacenado,
  output ready,
  output [7:0] Valor_seleccionado,
  output [3:0] \nº_bits_en_1 
);

  wire Reloj_out;
  wire [3:0] adder_1_out, multiplexer_3_out;
  wire [7:0] multiplexer_2_out, RegX_q, shifter_1_out;

  Clock u_Reloj (.out(Reloj_out));
  Register #(.trigger("falling")) Registro (
    .D(Entrada), .en(Escribir), .Q(Valor_almacenado), .clk(Reloj_out));  // open: clr
  Multiplexer #(.width(8), .disabled(0), .enable("false")) multiplexer_1 (
    .in0(Entrada_0), .in1(Entrada_1), .out(Valor_seleccionado), .sel(Selector));
  Shifter #(.shift("lr")) shifter_1 (.in(RegX_q), .\dist (3'b001), .out(shifter_1_out));
  Multiplexer #(.width(8), .disabled(0), .enable("false")) multiplexer_2 (
    .in0(shifter_1_out), .in1(x), .out(multiplexer_2_out), .sel(start));
  Adder #(.width(4)) adder_1 (.a(\nº_bits_en_1 ), .b(4'b0000), .out(adder_1_out), .cin(RegX_q[0]));  // open: cout
  Multiplexer #(.width(4), .disabled(0), .enable("false")) multiplexer_3 (
    .in0(adder_1_out), .in1(4'b0000), .out(multiplexer_3_out), .sel(start));
  Register #(.trigger("falling")) RegX (.D(multiplexer_2_out), .Q(RegX_q), .clk(reloj));  // open: en, clr
  Register #(.width(4), .trigger("falling")) RegCnt (
    .D(multiplexer_3_out), .Q(\nº_bits_en_1 ), .clk(reloj));  // open: en, clr
  // Probe on RegX_q
  Comparator comparator_1 (.a(RegX_q), .b({8{1'b0}}), .eq(ready));  // open: gt, lt

  // Notes on the sheet:
  //   Multiplexor
  //   Elementos modulares
  //   Son las variables locales
  //   de los circuitos
  //   Se modifica en el pulso
  //   de bajada del reloj
  //   si escribir está en 1
  //   Son los if en un circuito
  //   Entradas
  //   int contar(int x) {
  //   int cnt= 0;
  //   while (x!=0) {
  //   x = x>>1;
  //   }
  //   return cnt;
  //   }
  //   cnt += x&1;
  //   Ejemplo: contar los bits en 1
  //   Separador
  //   Salidas
endmodule

module mcd (
  input  [7:0] x,
  input  start,
  input  [7:0] y,
  input  reloj,
  output [7:0] mcd,
  output ready
);

  wire comparator_1_gt, comparator_1_lt, or_1_out, or_2_out;
  wire [7:0] multiplexer_1_out, multiplexer_2_out, RegX_2_q, subtractor_1_out, subtractor_2_out;

  Subtractor subtractor_1 (.a(mcd), .b(RegX_2_q), .out(subtractor_1_out));  // open: bin, bout
  Subtractor subtractor_2 (.a(RegX_2_q), .b(mcd), .out(subtractor_2_out));  // open: bin, bout
  Multiplexer #(.width(8), .disabled(0), .enable("false")) multiplexer_1 (
    .in0(subtractor_1_out), .in1(x), .out(multiplexer_1_out), .sel(start));
  Multiplexer #(.width(8), .disabled(0), .enable("false")) multiplexer_2 (
    .in0(subtractor_2_out), .in1(y), .out(multiplexer_2_out), .sel(start));
  // Probe on multiplexer_1_out
  or or_1 (or_1_out, comparator_1_gt, start);
  // Probe on multiplexer_2_out
  or or_2 (or_2_out, start, comparator_1_lt);
  Register #(.trigger("falling")) RegX (.D(multiplexer_1_out), .en(or_1_out), .Q(mcd), .clk(reloj));  // open: clr
  Register #(.trigger("falling")) RegX_2 (
    .D(multiplexer_2_out), .en(or_2_out), .Q(RegX_2_q), .clk(reloj));  // open: clr
  Comparator comparator_1 (.a(mcd), .b(RegX_2_q), .gt(comparator_1_gt), .eq(ready), .lt(comparator_1_lt));

  // Notes on the sheet:
  //   x - y
  //   y - x
  //   Ejemplo: calcular máximo común denominador
  //   }
  //   return x;
  //   }
  //   int mcd(int x, int y) {
  //   while (x!=y) {
  //   if (x>y) x = x - y;
  //   else y = y -x;
endmodule

module memorias_ROM (
  input  [7:0] \dirección ,
  input  start,
  input  [7:0] x,
  output [7:0] Valor_almacenado,
  output not_found,
  output found
);

  wire and_1_out, clock_1_out, or_1_out;
  wire [7:0] adder_1_out, multiplexer_1_out, RegCnt_q, rom_2_data;

  Clock clock_1 (.out(clock_1_out));
  Adder adder_1 (.a(RegCnt_q), .b(8'h1), .out(adder_1_out));  // open: cin, cout
  Multiplexer #(.width(8), .disabled(0), .enable("false")) multiplexer_1 (
    .in0(adder_1_out), .in1({8{1'b0}}), .out(multiplexer_1_out), .sel(start));
  ROM rom_1 (.addr(\dirección ), .data(Valor_almacenado));  // open: sel
  or or_1 (or_1_out, start, and_1_out);
  Register #(.trigger("falling")) RegCnt (
    .D(multiplexer_1_out), .en(or_1_out), .Q(RegCnt_q), .clk(clock_1_out));  // open: clr
  // Probe on Valor_almacenado
  // Probe on RegCnt_q
  Comparator comparator_1 (.a(RegCnt_q), .b({8{1'b1}}), .eq(not_found));  // open: gt, lt
  and and_1 (and_1_out, ~not_found, ~found);  // AND_Gate
  ROM rom_2 (.addr(RegCnt_q), .data(rom_2_data));  // open: sel
  Comparator comparator_2 (.a(x), .b(rom_2_data), .eq(found));  // open: gt, lt

  // Notes on the sheet:
  //   Ejemplo: buscar un número en la ROM
  //   Son tablas de lectura en los circuitos
  //   Memorias ROM
  //   contents of rom_1 (hex, n*v repeats v):
  //   3 5 7 b d 11 13 17 1d 1f 25 29 2b 2f 35 3b 3d
  //   contents of rom_2 (hex, n*v repeats v):
  //   3 5 7 b d 11 13 17 1d 1f 25 29 2b 2f 35 3b 3d
  //   }
  //   }
  //   int buscar(int x) {
  //   int cnt= 0;
  //   while (cnt!=255) {
  //   return 0;
  //   if (rom[cnt]==x) return 1;
endmodule

module memorias_RAM (
  input  [7:0] \dirección ,
  input  [7:0] entrada,
  input  escribir,
  input  reloj,
  input  start,
  input  [7:0] x,
  input  add,
  output [7:0] Valor_almacenado,
  output not_found,
  output found
);

  wire and_1_out, clock_1_out, not_1_out, not_2_out, or_1_out;
  wire [7:0] adder_1_out, adder_2_out, multiplexer_1_out, multiplexer_2_out, ram_2_data, RegCnt_q, RegNext_q;

  Clock clock_1 (.out(clock_1_out));
  // Probe on entrada
  Adder adder_1 (.a(RegCnt_q), .b(8'h1), .out(adder_1_out));  // open: cin, cout
  not not_1 (not_1_out, reloj);
  or or_1 (or_1_out, start, and_1_out);
  Multiplexer #(.width(8), .disabled(0), .enable("false")) multiplexer_1 (
    .in0(adder_1_out), .in1({8{1'b0}}), .out(multiplexer_1_out), .sel(start));
  Adder adder_2 (.a(8'h1), .b(RegNext_q), .out(adder_2_out));  // open: cin, cout
  RAM #(.bus("separate")) ram_1 (
    .addr(\dirección ), .din(entrada), .data(Valor_almacenado), .str(escribir), .clk(not_1_out));  // open: sel, ld, clr
  Register #(.trigger("falling")) RegCnt (
    .D(multiplexer_1_out), .en(or_1_out), .Q(RegCnt_q), .clk(clock_1_out));  // open: clr
  // Probe on RegCnt_q
  Register #(.trigger("falling")) RegNext (.D(adder_2_out), .en(add), .Q(RegNext_q), .clk(clock_1_out));  // open: clr
  // Probe on Valor_almacenado
  Multiplexer #(.width(8), .disabled(0), .enable("false")) multiplexer_2 (
    .in0(RegCnt_q), .in1(RegNext_q), .out(multiplexer_2_out), .sel(add));
  Comparator #(.mode("unsigned")) comparator_1 (.a(RegCnt_q), .b(RegNext_q), .eq(not_found));  // open: gt, lt
  and and_1 (and_1_out, ~not_found, ~found);  // AND_Gate
  RAM #(.bus("separate")) ram_2 (
    .addr(multiplexer_2_out), .din(x), .data(ram_2_data), .str(add), .clk(not_2_out));  // open: sel, ld, clr
  not not_2 (not_2_out, clock_1_out);
  Comparator comparator_2 (.a(x), .b(ram_2_data), .eq(found));  // open: gt, lt
  ROM rom_1 ();  // open: addr, data, sel

  // Notes on the sheet:
  //   buscar
  //   agregar
  //   Ejemplo: agregar o buscar
  //   un número en la RAM
  //   Memorias RAM
  //   Son los arreglos en los circuitos
  //   RAM
  //   }
  //   }
  //   }
  //   contents of rom_1 (hex, n*v repeats v):
  //   3 5 7 b d 11 13 17 1d 1f 25 29 2b 2f 35 3b 3d
  //   int next= 0;
  //   int ram[256];
  //   int buscar(int x) {
  //   int cnt= 0;
  //   while (cnt!=next) {
  //   return 0;
  //   int agregar(int x) {
  //   ram[next++]= x;
  //   if (ram[cnt]==x) return 1;
endmodule
